// Logisim project bt1.circ as structural Verilog: 1 circuit, main circuit main
module main (
  input  A,
  input  B,
  output out_3,
  output out_4,
  output out_5,
  output out_6,
  output out_7,
  output out_8,
  output out_9
);

  xnor xnor_1 (out_3, A, B);
  nor nor_1 (out_5, A, B);
  nand nand_1 (out_4, A, B);
  and and_1 (out_6, A, B);
  or or_1 (out_7, A, B);
  not not_1 (out_8, B);
  xor xor_1 (out_9, A, B);
endmodule
