// Logisim project nhap.circ as structural Verilog: 1 circuit, main circuit main
module main (
  input  A,
  input  B,
  input  C,
  input  D,
  output A_o,
  output B_o,
  output C_o,
  output D_o
);

  wire Clock_out;

  Clock Clock (.out(Clock_out));
  Register #(.width(4)) Thanh_ghi (
    .D({D, C, B, A}), .en(1'b1), .Q({D_o, C_o, B_o, A_o}), .clk(Clock_out));  // open: clr

  // Notes on the sheet:
  //   Ngõ vào
  //   Ngõ ra
endmodule
