// Logisim project ALU_01.circ as structural Verilog: 1 circuit, main circuit main
module main (
  input  [1:0] \Ngõ_vào_điều_khiển ,
  input  [7:0] A,
  input  [7:0] B,
  output [7:0] \Ngõ_ra 
);

  wire [7:0] adder_1_out, AND_out, NAND_out, subtractor_1_out;

  Adder adder_1 (.a(A), .b(B), .out(adder_1_out));  // open: cin, cout
  Subtractor subtractor_1 (.a(A), .b(B), .out(subtractor_1_out));  // open: bin, bout
  assign AND_out = A & B;  // AND_Gate AND, 8 bits wide
  assign NAND_out = ~(A & B);  // NAND_Gate NAND, 8 bits wide
  Multiplexer #(.select(2), .width(8)) multiplexer_1 (
    .in0(adder_1_out), .in1(subtractor_1_out), .in2(AND_out), .in3(NAND_out), .out(\Ngõ_ra ),
    .sel(\Ngõ_vào_điều_khiển ));  // open: en

  // Notes on the sheet:
  //   Ngõ vào dữ liệu
endmodule
