// Logisim project ALU_Upgraded.circ as structural Verilog: 1 circuit, main circuit main
module main (
  input  [7:0] A,
  input  [2:0] \Ngõ_vào_điều_khiển ,
  input  [7:0] B,
  output [7:0] \Ngõ_ra 
);

  wire [7:0] adder_1_out, adder_2_out, AND_out, not_1_out, OR_out, subtractor_1_out, subtractor_2_out,
       XOR_out;

  assign not_1_out = ~A;  // NOT_Gate not_1, 8 bits wide
  Adder adder_1 (.a(A), .b(B), .out(adder_1_out));  // open: cin, cout
  Adder adder_2 (.a(A), .b(8'h1), .out(adder_2_out));  // open: cin, cout
  Subtractor subtractor_1 (.a(A), .b(B), .out(subtractor_1_out));  // open: bin, bout
  Subtractor subtractor_2 (.a(A), .b(8'h1), .out(subtractor_2_out));  // open: bin, bout
  assign AND_out = A & B;  // AND_Gate AND, 8 bits wide
  assign OR_out = A | B;  // OR_Gate OR, 8 bits wide
  assign XOR_out = A ^ B;  // XOR_Gate XOR, 8 bits wide
  Multiplexer #(.select(3), .width(8)) multiplexer_1 (
    .in0(adder_1_out), .in1(adder_2_out), .in2(subtractor_1_out), .in3(subtractor_2_out), .in4(AND_out),
    .in5(OR_out), .in6(not_1_out), .in7(XOR_out), .out(\Ngõ_ra ), .sel(\Ngõ_vào_điều_khiển ));  // open: en

  // Notes on the sheet:
  //   Ngõ vào dữ liệu
endmodule
